// Logisim project cpu.circ as structural Verilog: 2 circuits, main circuit main
module main (
  input  [31:0] INSTRUCTION,
  input  CLOCK,
  output [31:0] PROGRAM_COUNTER,
  output [31:0] ra,
  output [31:0] sp,
  output [31:0] t0,
  output [31:0] t1,
  output [31:0] t2,
  output [31:0] s0,
  output [31:0] s1,
  output [31:0] a0
);

  wire control_logic_1_bsel, control_logic_1_memrw, control_logic_1_regwen;
  wire [1:0] control_logic_1_wbsel;
  wire [2:0] control_logic_1_immsel;
  wire [3:0] control_logic_1_alusel;
  wire [4:0] rdUse, rs1Use, rs2Use;
  wire [31:0] adder_1_out, Arithmetic_Logic_Unit_result, DMEM_p4, immOut, INSTRUCTION_USE, multiplexer_1_out,
       RegFile_read_data_1, RegFile_read_data_2, wbUse;

  control_logic control_logic_1 (
    .BSel(control_logic_1_bsel), .RegWEn(control_logic_1_regwen), .ImmSel(control_logic_1_immsel),
    .inst(INSTRUCTION_USE), .ALUSel(control_logic_1_alusel), .MemRW(control_logic_1_memrw),
    .WBSel(control_logic_1_wbsel));  // open: BrUn, ASel, PCSel, BrLt, BrEq
  Adder #(.width(32)) adder_1 (.a(PROGRAM_COUNTER), .b(32'h4), .out(adder_1_out));  // open: cin, cout
  Register #(.width(32)) PC (.D(adder_1_out), .clk(CLOCK), .Q(PROGRAM_COUNTER));  // open: en, clr
  imm_gen imm_gen_1 (.ImmSel(control_logic_1_immsel), .inst(INSTRUCTION_USE), .imm(immOut));
  Register #(.width(32)) register_1 (.D(INSTRUCTION), .en(1'b1), .clk(CLOCK), .Q(INSTRUCTION_USE));  // open: clr
  // Probe on INSTRUCTION_USE
  // branch_comp branch_comp_1: pin names not known
  regfile_main RegFile (
    .rs2(rs2Use), .rd(rdUse), .Read_Data_1(RegFile_read_data_1), .Read_Data_2(RegFile_read_data_2), .ra(ra),
    .sp(sp), .t0(t0), .t1(t1), .t2(t2), .s0(s0), .s1(s1), .a0(a0), .rs1(rs1Use), .Write_Data(wbUse),
    .RegWEn(1'b1), .clk(CLOCK));
  InsParse insparse_1 (.in_1(INSTRUCTION_USE), .rd(rdUse), .rs1(rs1Use), .rs2(rs2Use));  // open: opcode, funct3, funct7
  Multiplexer #(.width(32), .enable("false")) multiplexer_1 (
    .in0(RegFile_read_data_2), .in1(immOut), .out(multiplexer_1_out), .sel(1'b1));
  alu Arithmetic_Logic_Unit (
    .Result(Arithmetic_Logic_Unit_result), .ALUSel(control_logic_1_alusel), .A(RegFile_read_data_1),
    .B(multiplexer_1_out));
  // mem_main DMEM: pin names not known; wires that end beside it: Arithmetic_Logic_Unit_result, CLOCK, control_logic_1_memrw, DMEM_p4
  Multiplexer #(.select(2), .width(32), .enable("false")) multiplexer_2 (
    .in0(Arithmetic_Logic_Unit_result), .in1(DMEM_p4), .in2(immOut), .out(wbUse), .sel(control_logic_1_wbsel));  // open: in3

  // Other names for the same wires on the sheet: clk = CLOCK

  // Notes on the sheet:
  //   Output
  //   IMEM (do **NOT** move this)
  //   Inputs
  //   It is OK to move the PC, RegFile, ALU, MEM, Branch Comp, Imm Gen, and Control Logic to wherever is most convenient for you when constructing your CPU, and to delete this text
  //   Inputs/Outputs for testing. Do **NOT** move these.
endmodule

module InsParse (
  input  [31:0] in_1,
  output [6:0] opcode,
  output [4:0] rd,
  output [2:0] funct3,
  output [4:0] rs1,
  output [4:0] rs2,
  output [6:0] funct7
);


  assign funct3 = in_1[14:12];
  assign funct7 = in_1[31:25];
  assign opcode = in_1[6:0];
  assign rd = in_1[11:7];
  assign rs1 = in_1[19:15];
  assign rs2 = in_1[24:20];
endmodule
